// Logisim project c3200a.circ as structural Verilog: 8 circuits, main circuit main
module main (
);

  wire and_1_out, and_2_out, and_3_out, button_1_out, clock_1_out, clocker_1_p0, clocker_1_p1, clocker_1_p2,
       clocker_1_p3, clocker_1_p5, d_ff_1_q, d_ff_2_q, d_ff_3_q, d_ff_4_q, d_ff_5_q, d_ff_6_q, d_ff_7_q,
       d_ff_8_q, decode_1_alue, decode_1_immhigh, decode_1_memr, decode_1_memw, decode_1_pcw, decode_1_regw,
       jumper_1_jump, or_1_out, or_2_out, or_3_out, or_4_out, undriven;
  wire [2:0] decode_1_aluop, decode_1_dbussel;
  wire [3:0] decode_1_asel, decode_1_bsel, decode_1_dsel;
  wire [3:3] decode_1_aluop_2;
  wire [7:0] alu_1_cout, flags_q, memory_1_led;
  wire [15:0] decode_1_imm, imm_q;
  wire [23:0] multiplexer_1_out, pc_q, regfile_1_a, regfile_1_b;
  wire [31:0] alu_1_d, immmov_1_immout, inst_q, memory_1_dataout, multiplexer_2_out;
  wire [31:24] regfile_1_a_2, regfile_1_b_2;

  Register #(.width(32)) inst (.D(memory_1_dataout), .clk(clocker_1_p2), .Q(inst_q));  // open: en, clr
  Clock clock_1 (.out(clock_1_out));
  or or_1 (or_1_out, clock_1_out, button_1_out);
  Button button_1 (.out(button_1_out));
  clocker clocker_1 (
    .skip(undriven), .clk(or_1_out), .p0(clocker_1_p0), .p1(clocker_1_p1), .p2(clocker_1_p2),
    .p3(clocker_1_p3), .p5(clocker_1_p5));  // open: p4
  decode decode_1 (
    .inst(inst_q), .asel(decode_1_asel), .bsel(decode_1_bsel), .dsel(decode_1_dsel),
    .dbussel(decode_1_dbussel), .regw(decode_1_regw), .pcw(decode_1_pcw), .memr(decode_1_memr),
    .memw(decode_1_memw), .alue(decode_1_alue), .aluop({decode_1_aluop_2[3], decode_1_aluop}),
    .immhigh(decode_1_immhigh), .imm(decode_1_imm));
  Register #(.width(16)) imm (.D(decode_1_imm), .clk(clocker_1_p3), .Q(imm_q));  // open: en, clr
  and and_1 (and_1_out, decode_1_pcw, jumper_1_jump, clocker_1_p5);
  or or_2 (or_2_out, clocker_1_p0, clocker_1_p1);
  or or_3 (or_3_out, clocker_1_p2, and_1_out);
  Counter #(.width(24), .max('hffffff)) pc (
    .load(decode_1_pcw), .clk(or_3_out), .D(regfile_1_a), .Q(pc_q));  // open: clr, up, count, carry
  immmov immmov_1 (.a({regfile_1_a_2, regfile_1_a}), .immin(imm_q), .high(decode_1_immhigh), .immout(immmov_1_immout));
  and and_2 (and_2_out, clocker_1_p5, decode_1_memw);
  regfile regfile_1 (
    .asel(decode_1_asel), .bsel(decode_1_bsel), .dsel(decode_1_dsel), .d(multiplexer_2_out),
    .regw(decode_1_regw), .rclk(clocker_1_p3), .wclk(clocker_1_p5), .a({regfile_1_a_2, regfile_1_a}),
    .b({regfile_1_b_2, regfile_1_b}));
  Multiplexer #(.width(24), .enable("false")) multiplexer_1 (
    .in0(regfile_1_b), .in1(pc_q), .out(multiplexer_1_out), .sel(or_2_out));
  or or_4 (or_4_out, decode_1_memr, clocker_1_p5, clocker_1_p1);
  Multiplexer #(.select(3), .width(32), .enable("false")) multiplexer_2 (
    .in0(immmov_1_immout), .in1({regfile_1_a_2, regfile_1_a}), .in2(memory_1_dataout), .in3(alu_1_d),
    .in4({{24{1'b0}}, flags_q}), .out(multiplexer_2_out), .sel(decode_1_dbussel));  // open: in5, in6, in7
  memory memory_1 (
    .addr(multiplexer_1_out), .datain({regfile_1_a_2, regfile_1_a}), .wen(and_2_out), .ren(or_4_out),
    .clk(or_4_out), .dataout(memory_1_dataout), .led(memory_1_led));
  and and_3 (and_3_out, decode_1_alue, clocker_1_p5);
  D_Flip_Flop d_ff_1 (.D(memory_1_led[0]), .clk(clock_1_out), .Q(d_ff_1_q));  // open: Qn, preset, reset
  D_Flip_Flop d_ff_2 (.D(memory_1_led[1]), .clk(clock_1_out), .Q(d_ff_2_q));  // open: Qn, preset, reset
  D_Flip_Flop d_ff_3 (.D(memory_1_led[2]), .clk(clock_1_out), .Q(d_ff_3_q));  // open: Qn, preset, reset
  D_Flip_Flop d_ff_4 (.D(memory_1_led[3]), .clk(clock_1_out), .Q(d_ff_4_q));  // open: Qn, preset, reset
  D_Flip_Flop d_ff_5 (.D(memory_1_led[4]), .clk(clock_1_out), .Q(d_ff_5_q));  // open: Qn, preset, reset
  D_Flip_Flop d_ff_6 (.D(memory_1_led[5]), .clk(clock_1_out), .Q(d_ff_6_q));  // open: Qn, preset, reset
  D_Flip_Flop d_ff_7 (.D(memory_1_led[6]), .clk(clock_1_out), .Q(d_ff_7_q));  // open: Qn, preset, reset
  D_Flip_Flop d_ff_8 (.D(memory_1_led[7]), .clk(clock_1_out), .Q(d_ff_8_q));  // open: Qn, preset, reset
  alu alu_1 (
    .cin(flags_q[0]), .a({regfile_1_a_2, regfile_1_a}), .b({regfile_1_b_2, regfile_1_b}),
    .aluop({decode_1_aluop_2[3], decode_1_aluop}), .d(alu_1_d), .cout(alu_1_cout[0]), .zout(alu_1_cout[1]),
    .sout(alu_1_cout[2]));
  LED led_1 (.in(d_ff_1_q));
  LED led_2 (.in(d_ff_2_q));
  LED led_3 (.in(d_ff_3_q));
  Register flags (.D(alu_1_cout), .clk(and_3_out), .Q(flags_q));  // open: en, clr
  jumper jumper_1 (.jmpop(decode_1_aluop), .flags(flags_q), .jump(jumper_1_jump));
  LED led_4 (.in(d_ff_4_q));
  LED led_5 (.in(d_ff_7_q));
  LED led_6 (.in(d_ff_6_q));
  LED led_7 (.in(d_ff_5_q));
  LED led_8 (.in(d_ff_8_q));
endmodule

module decode (
  input  [31:0] inst,
  output [3:0] asel,
  output [3:0] bsel,
  output [3:0] dsel,
  output [2:0] dbussel,
  output regw,
  output pcw,
  output memr,
  output memw,
  output alue,
  output [3:0] aluop,
  output immhigh,
  output [15:0] imm
);

  wire decoder_2_out0, decoder_2_out2;

  Decoder #(.select(3), .enable("false")) decoder_1 (
    .out1(alue), .out2(pcw), .sel(inst[31:29]));  // open: out0, out3, out4, out5, out6, out7
  Decoder #(.select(3), .enable("false")) decoder_2 (
    .out0(decoder_2_out0), .out1(immhigh), .out2(decoder_2_out2), .out3(memr), .out4(memw), .sel(inst[22:20]));  // open: out5, out6, out7
  or or_1 (regw, decoder_2_out0, immhigh, alue, decoder_2_out2, memr);

  assign aluop = inst[23:20];
  assign asel = inst[3:0];
  assign bsel = inst[7:4];
  assign dbussel = inst[28:26];
  assign dsel = inst[19:16];
  assign imm = inst[15:0];

  // Notes on the sheet:
  //   imm
  //   a
  //   b
  //   d
  //   notop
  //   op
  //   dbus
  //   funcsel
  //   oplow
  //   aluop
endmodule

module regfile (
  input  [3:0] asel,
  input  [3:0] bsel,
  input  [3:0] dsel,
  input  [31:0] d,
  input  regw,
  input  rclk,
  input  wclk,
  output [31:0] a,
  output [31:0] b
);

  wire decoder_1_out0, decoder_1_out1, decoder_1_out2, decoder_1_out3, decoder_1_out4, decoder_1_out5,
       decoder_1_out6, decoder_1_out7, decoder_1_out8, decoder_1_out9, decoder_1_out10, decoder_1_out11,
       decoder_1_out12, decoder_1_out13, decoder_1_out14, decoder_1_out15, undriven;
  wire [31:0] multiplexer_1_out, multiplexer_2_out, r0_q, r1_q, r2_q, r3_q, r4_q, r5_q, r6_q, r7_q, r8_q,
       r9_q, r10_q, r11_q, r12_q, r13_q, r14_q, r15_q;

  Decoder #(.select(4)) decoder_1 (
    .out0(decoder_1_out0), .out1(decoder_1_out1), .out2(decoder_1_out2), .out3(decoder_1_out3),
    .out4(decoder_1_out4), .out5(decoder_1_out5), .out6(decoder_1_out6), .out7(decoder_1_out7),
    .out8(decoder_1_out8), .out9(decoder_1_out9), .out10(decoder_1_out10), .out11(decoder_1_out11),
    .out12(decoder_1_out12), .out13(decoder_1_out13), .out14(decoder_1_out14), .out15(decoder_1_out15),
    .sel(dsel), .en(regw));
  Register #(.width(32)) r0 (.D(d), .en(decoder_1_out0), .clk(wclk), .Q(r0_q));  // open: clr
  Register #(.width(32)) r1 (.D(d), .en(decoder_1_out1), .clk(wclk), .Q(r1_q), .clr(undriven));
  Register #(.width(32)) r2 (.D(d), .en(decoder_1_out2), .clk(wclk), .Q(r2_q));  // open: clr
  Register #(.width(32)) r3 (.D(d), .en(decoder_1_out3), .clk(wclk), .Q(r3_q));  // open: clr
  Register #(.width(32)) r4 (.D(d), .en(decoder_1_out4), .clk(wclk), .Q(r4_q));  // open: clr
  Register #(.width(32)) r5 (.D(d), .en(decoder_1_out5), .clk(wclk), .Q(r5_q));  // open: clr
  Register #(.width(32)) r6 (.D(d), .en(decoder_1_out6), .clk(wclk), .Q(r6_q));  // open: clr
  Register #(.width(32)) r7 (.D(d), .en(decoder_1_out7), .clk(wclk), .Q(r7_q));  // open: clr
  Register #(.width(32)) r8 (.D(d), .en(decoder_1_out8), .clk(wclk), .Q(r8_q));  // open: clr
  Register #(.width(32)) r9 (.D(d), .en(decoder_1_out9), .clk(wclk), .Q(r9_q));  // open: clr
  Register #(.width(32)) r10 (.D(d), .en(decoder_1_out10), .clk(wclk), .Q(r10_q));  // open: clr
  Register #(.width(32)) r11 (.D(d), .en(decoder_1_out11), .clk(wclk), .Q(r11_q));  // open: clr
  Register #(.width(32)) r12 (.D(d), .en(decoder_1_out12), .clk(wclk), .Q(r12_q));  // open: clr
  Register #(.width(32)) r13 (.D(d), .en(decoder_1_out13), .clk(wclk), .Q(r13_q));  // open: clr
  Register #(.width(32)) r14 (.D(d), .en(decoder_1_out14), .clk(wclk), .Q(r14_q));  // open: clr
  Register #(.width(32)) r15 (.D(d), .en(decoder_1_out15), .clk(wclk), .Q(r15_q));  // open: clr
  Multiplexer #(.select(4), .width(32), .enable("false")) multiplexer_1 (
    .in0(r0_q), .in1(r1_q), .in2(r2_q), .in3(r3_q), .in4(r4_q), .in5(r5_q), .in6(r6_q), .in7(r7_q),
    .in8(r8_q), .in9(r9_q), .in10(r10_q), .in11(r11_q), .in12(r12_q), .in13(r13_q), .in14(r14_q),
    .in15(r15_q), .out(multiplexer_1_out), .sel(asel));
  Multiplexer #(.select(4), .width(32), .enable("false")) multiplexer_2 (
    .in0(r0_q), .in1(r1_q), .in2(r2_q), .in3(r3_q), .in4(r4_q), .in5(r5_q), .in6(r6_q), .in7(r7_q),
    .in8(r8_q), .in9(r9_q), .in10(r10_q), .in11(r11_q), .in12(r12_q), .in13(r13_q), .in14(r14_q),
    .in15(r15_q), .out(multiplexer_2_out), .sel(bsel));
  Register #(.width(32)) abuf (.D(multiplexer_1_out), .clk(rclk), .Q(a));  // open: en, clr
  Register #(.width(32)) bbuf (.D(multiplexer_2_out), .clk(rclk), .Q(b));  // open: en, clr
endmodule

module clocker (
  input  skip,
  input  clk,
  output p0,
  output p1,
  output p2,
  output p3,
  output p4,
  output p5
);

  wire d_ff_1_qn, shift_register_1_p3;

  D_Flip_Flop d_ff_1 (.D(1'b1), .clk(p0), .Qn(d_ff_1_qn));  // open: Q, preset, reset
  // Shift_Register #(.length(6)) shift_register_1: pin names not known; wires that end beside it: skip, clk, shift_register_1_p3, 1'b1, 1'b0, 1'b0, 1'b0, 1'b0, 1'b0, p0, p1, p2, p3, p4, p5
  Multiplexer #(.enable("false")) multiplexer_1 (.in0(p5), .in1(d_ff_1_qn), .out(shift_register_1_p3), .sel(d_ff_1_qn));
endmodule

module immmov (
  input  [31:0] a,
  input  [15:0] immin,
  input  high,
  output [31:0] immout
);

  Multiplexer #(.width(32), .enable("false")) multiplexer_1 (
    .in0({a[31:16], immin}), .in1({immin, a[15:0]}), .out(immout), .sel(high));
endmodule

module alu (
  input  cin,
  input  [31:0] a,
  input  [31:0] b,
  input  [3:0] aluop,
  output [31:0] d,
  output cout,
  output zout,
  output sout
);

  wire adder_1_cout, subtractor_1_bout;
  wire [30:0] multiplier_1_out;
  wire [31:0] adder_1_out, and_1_out, and_2_out, divider_1_out, divider_1_rem, multiplexer_2_out,
       negator_1_out, not_1_out, or_1_out, shifter_1_out, shifter_2_out, shifter_3_out, subtractor_1_out,
       subtractor_2_out, xor_1_out;
  wire [31:31] undriven;

  Adder #(.width(32)) adder_1 (.a(a), .b(b), .out(adder_1_out), .cin(cin), .cout(adder_1_cout));
  Subtractor #(.width(32)) subtractor_1 (.a(a), .b(b), .out(subtractor_1_out), .bin(cin), .bout(subtractor_1_bout));
  Multiplier #(.width(31)) multiplier_1 (.a(a[30:0]), .b(b[30:0]), .out(multiplier_1_out));  // open: cin, cout
  Divider #(.width(32)) divider_1 (.a(a), .b(b), .out(divider_1_out), .rem(divider_1_rem));  // open: upper
  Negator #(.width(32)) negator_1 (.in(a), .out(negator_1_out));
  assign and_1_out = a & b;  // AND_Gate and_1, 32 bits wide
  assign or_1_out = a | b;  // OR_Gate or_1, 32 bits wide
  assign xor_1_out = a ^ b;  // XOR_Gate xor_1, 32 bits wide
  assign not_1_out = ~a;  // NOT_Gate not_1, 32 bits wide
  Shifter #(.width(32)) shifter_1 (.in(a), .\dist (b[4:0]), .out(shifter_1_out));
  Shifter #(.width(32), .shift("lr")) shifter_2 (.in(a), .\dist (b[4:0]), .out(shifter_2_out));
  Shifter #(.width(32), .shift("ar")) shifter_3 (.in(a), .\dist (b[4:0]), .out(shifter_3_out));
  Subtractor #(.width(32)) subtractor_2 (.a(a), .b(b), .out(subtractor_2_out));  // open: bin, bout
  assign and_2_out = a & b;  // AND_Gate and_2, 32 bits wide
  Multiplexer #(.select(4), .width(32), .enable("false")) multiplexer_1 (
    .in0(adder_1_out), .in1(subtractor_1_out), .in2({undriven[31], multiplier_1_out}), .in3(divider_1_out),
    .in4(divider_1_rem), .in5(negator_1_out), .in6(and_1_out), .in7(or_1_out), .in8(xor_1_out),
    .in9(not_1_out), .in10(shifter_1_out), .in11(shifter_2_out), .in12(shifter_3_out), .out(d), .sel(aluop));  // open: in13, in14, in15
  Multiplexer #(.select(4), .width(32), .enable("false")) multiplexer_2 (
    .in0(adder_1_out), .in1(subtractor_1_out), .in2({undriven[31], multiplier_1_out}), .in3(divider_1_out),
    .in4(divider_1_rem), .in5(negator_1_out), .in6(and_1_out), .in7(or_1_out), .in8(xor_1_out),
    .in9(not_1_out), .in10(shifter_1_out), .in11(shifter_2_out), .in12(shifter_3_out),
    .in13(subtractor_2_out), .in14(and_2_out), .out(multiplexer_2_out));  // open: in15, sel
  Multiplexer #(.select(4), .enable("false")) multiplexer_3 (
    .in0(adder_1_cout), .in1(subtractor_1_bout), .out(cout), .sel(aluop));  // open: in2, in3, in4, in5, in6, in7, in8, in9, in10, in11, in12, in13, in14, in15
  Comparator #(.width(32)) comparator_1 (.a(multiplexer_2_out), .b({32{1'b0}}), .eq(zout), .lt(sout));  // open: gt
  Pull_Resistor pull_resistor_1 (.node(cout));
  Pull_Resistor pull_resistor_2 (.node(zout));
  Pull_Resistor pull_resistor_3 (.node(sout));
endmodule

module jumper (
  input  [2:0] jmpop,
  input  [7:0] flags,
  output jump
);

  wire and_1_out, and_2_out, and_3_out, and_4_out, decoder_1_out0, decoder_1_out1, decoder_1_out2,
       decoder_1_out3, decoder_1_out4;

  Decoder #(.select(3), .enable("false")) decoder_1 (
    .out0(decoder_1_out0), .out1(decoder_1_out1), .out2(decoder_1_out2), .out3(decoder_1_out3),
    .out4(decoder_1_out4), .sel(jmpop));  // open: out5, out6, out7
  and and_1 (and_1_out, decoder_1_out1, flags[1]);
  and and_2 (and_2_out, decoder_1_out2, ~flags[1]);  // AND_Gate
  and and_3 (and_3_out, decoder_1_out3, ~flags[1], flags[2]);  // AND_Gate
  and and_4 (and_4_out, decoder_1_out4, ~flags[1], ~flags[2]);  // AND_Gate
  or or_1 (jump, decoder_1_out0, and_1_out, and_2_out, and_3_out, and_4_out);

  // Notes on the sheet:
  //   z
  //   s
endmodule

module memory (
  input  [23:0] addr,
  input  [31:0] datain,
  input  wen,
  input  ren,
  input  clk,
  output [31:0] dataout,
  output [7:0] led
);

  wire and_1_out, and_2_out, and_3_out, comparator_1_eq, comparator_1_gt, comparator_2_eq, comparator_2_lt,
       or_1_out, or_2_out;
  wire [31:0] demultiplexer_1_out0;
  wire [31:8] undriven;

  Comparator #(.width(24), .mode("unsigned")) comparator_1 (
    .a(addr), .b(24'hf00000), .gt(comparator_1_gt), .eq(comparator_1_eq));  // open: lt
  or or_1 (or_1_out, comparator_1_gt, comparator_1_eq);
  Comparator #(.width(24), .mode("unsigned")) comparator_2 (
    .a(addr), .b(24'hf00007), .eq(comparator_2_eq), .lt(comparator_2_lt));  // open: gt
  or or_2 (or_2_out, comparator_2_eq, comparator_2_lt);
  and and_1 (and_1_out, clk, and_3_out);
  and and_2 (and_2_out, clk, ~and_3_out);  // AND_Gate
  and and_3 (and_3_out, or_1_out, or_2_out);
  RAM #(.addrWidth(24), .dataWidth(32), .databus("bibus")) ram_1 (
    .addr(addr), .we(wen), .oe(ren), .clk(and_2_out), .din(datain), .dout(dataout));
  Demultiplexer #(.width(32), .enable("false")) demultiplexer_1 (
    .out0(demultiplexer_1_out0), .out1(datain), .in({undriven, led}), .sel(and_1_out));
endmodule
